# Fritzing sketch şematikçizim (saved by Fritzing 0.9.3b)
breadboards: 1

parts:
  Parça1 = Arduino Uno (Rev3)
  Raspberry_Pi_1 = Raspberry Pi 3 [part_number=RPI-3-V1.2]
  M1 = DC Motor  # not connected
  M2 = DC Motor
  DHT1 = DHT11 Humitidy and Temperature Sensor
  Parça4 = MQ-6 breakout
  R1 = Resistor [tolerance=±5% resistance=220 package=THT]

nets (from the schematic view):
  N1: Parça1.A0, Parça4.AO
  GND: Parça1.GND, Parça4.GND
  5V: Parça1.5V, Parça4.VCC
  3V3: Raspberry_Pi_1.3v3, DHT1.VDD, R1.Pin_0
  N2: Raspberry_Pi_1.GND, Raspberry_Pi_1.GPIO24, Raspberry_Pi_1.GPIO18, M2.pin_1, DHT1.NULL
  N3: Raspberry_Pi_1.GPIO14, DHT1.DATA, R1.Pin_1

notes:
  havalandırma motoru
  soğutma motoru

custom parts:
  DHT11 Humitidy and Temperature Sensor: DHT11 Humidity and Temperature Sensor
  MQ-6 breakout: SKU: 101282
